# Fritzing sketch arduino_uno_rev3_isp_to_atmega32a (saved by Fritzing 0.9.6b)
breadboards: 1

parts:
  Componente1 = Arduino Uno (Rev3)
  µC1 = ATmega32 [package=dip]

nets:
  N1: Componente1.D10_PWM/SS, µC1.RESET
  N2: Componente1.D11_PWM/MOSI, µC1.PB5
  N3: Componente1.D12/MISO, µC1.PB6
  N4: Componente1.D13/SCK, µC1.PB7
  5V: Componente1.5V, µC1.VCC, µC1.AVCC
  GND: Componente1.GND, µC1.GND1, µC1.GND2

custom parts:
  ATmega32: AVR 8-bit microcontroller.
